# Fritzing sketch weather-station-schematic (saved by Fritzing 0.8.3b)
breadboards: 2

parts:
  Composants1 = Arduino Uno (Rev3)  # not connected
  U1 = attiny85 [package=dip]
  DS18B20 = LM35 Temperature Sensor [package="TO92 [THT]"]
  LCD1 = LCD screen  # not connected
  RX = RF-LINK_RX [package=rf-link_rx]  # not connected
  TX = RF-LINK_TX [package=rf-link_tx]
  Composants2 = Barometric Pressure Sensor - BMP085 Breakout  # not connected
  AA_3 = Battery Holders [package=battery-aa-kit]
  AA_2 = Battery Holders [package=battery-aa-kit]
  AA_1 = Battery Holders [package=battery-aa-kit]
  ANT1 = Antenna
  TX_Led = LED - 5mm [color="Red (633nm)" package="5 mm [THT]"]
  R_PullUp = Resistor [tolerance=±5% resistance=4.7k package=THT]
  R1 = Resistor [tolerance=±5% resistance=2.2k package=THT]

nets:
  N1: U1.Pin_2, R1.Pin_0
  N2: U1.Pin_3, TX.+5V, R_PullUp.Pin_0
  GND: U1.Pin_4, DS18B20.GND, TX.GND, AA_1.+, TX_Led.cathode
  N3: U1.Pin_5, DS18B20.Vout, R_PullUp.Pin_1
  N4: U1.Pin_6, TX.DATA
  N5: U1.Pin_8, AA_3.-
  N6: TX.ANT, ANT1.antenna_lead
  N7: AA_3.+, AA_2.-
  N8: AA_2.+, AA_1.-
  N9: TX_Led.anode, R1.Pin_1
