# Fritzing sketch weather-station-schematic (saved by Fritzing 0.8.5b)
breadboards: 2

parts:
  U1 = attiny85 [package=dip]
  DS18B20 = LM35 Temperature Sensor [package="TO92 [THT]"]
  LCD1 = LCD screen
  RX = RF-LINK_RX [package=rf-link_rx]
  TX = RF-LINK_TX [package=rf-link_tx]
  BMP085 = Barometric Pressure Sensor - BMP085 Breakout
  AA_3 = Battery Holders [package=battery-aa-kit]
  AA_2 = Battery Holders [package=battery-aa-kit]
  AA_1 = Battery Holders [package=battery-aa-kit]
  ANT1 = Antenna
  TX_Led = LED - 5mm [color="Red (633nm)" package="5 mm [THT]"]
  R_PullUp = Resistor [tolerance=±5% resistance=4.7k package=THT]
  R1 = Resistor [tolerance=±5% resistance=2.2k package=THT]
  Main_Station = Arduino Uno (Rev3)
  Ethernet = ENC28J60 [package=ssop28db]
  Integrated_chip_with_LCD = PCF8575C [package=so-24dw]
  ANT2 = Antenna
  RX_LED = LED - 5mm [color="Blue (505nm)" package="5 mm [THT]"]
  Ethernet_LED = LED - 5mm [color="Red (633nm)" package="5 mm [THT]"]
  R2 = Resistor [tolerance=±5% resistance=2.2k package=THT]
  R3 = Resistor [tolerance=±5% resistance=2.2k package=THT]
  U2 = TOUCH [package=touch2]
  R5 = Resistor [tolerance=±5% resistance=1M package=THT]
  R6 = Resistor [tolerance=±5% resistance=1M package=THT]

nets:
  N1: U1.Pin_2, R1.Pin_0
  N2: U1.Pin_3, TX.+5V, R_PullUp.Pin_0
  GND: U1.Pin_4, DS18B20.GND, TX.GND, AA_1.+, TX_Led.cathode
  N3: U1.Pin_5, DS18B20.Vout, R_PullUp.Pin_1
  N4: U1.Pin_6, TX.DATA
  N5: U1.Pin_8, AA_3.-
  GND_2: LCD1.V0, RX.GND, BMP085.GND, Main_Station.GND, Integrated_chip_with_LCD.GND, RX_LED.cathode, RX_LED.anode, Ethernet_LED.cathode, R2.Pin_1
  N6: RX.DATA, Main_Station.D7
  N7: RX.ANT, ANT2.antenna_lead
  N8: TX.ANT, ANT1.antenna_lead
  N9: BMP085.SCL, Main_Station.A5/SCL, Integrated_chip_with_LCD.SCL
  N10: BMP085.SDA, Main_Station.A4/SDA, Integrated_chip_with_LCD.SDA
  N11: AA_3.+, AA_2.-
  N12: AA_2.+, AA_1.-
  N13: TX_Led.anode, R1.Pin_1
  N14: Main_Station.D8, Ethernet.CS
  N15: Main_Station.D11_PWM/MOSI, Ethernet.SI
  N16: Main_Station.D12/MISO, Ethernet.SO
  N17: Main_Station.D13/SCK, Ethernet.SCK
  N18: Main_Station.D2, R5.Pin_0
  N19: Main_Station.D4, U2.T1, R6.Pin_1
  N20: Main_Station.D5_PWM, R3.Pin_0
  N21: Main_Station.D6_PWM, R2.Pin_0
  N22: Main_Station.RESET, Ethernet.RESET
  N23: Ethernet_LED.anode, R3.Pin_1
  N24: R5.Pin_1, R6.Pin_0
